// Logisim project Circuit file with subcircuit.circ as structural Verilog: 2 circuits, main circuit main
module main (
  input  A1,
  input  B1,
  input  A2,
  input  B2,
  input  [1:0] S1_S2,
  output F1,
  output [1:0] out_7,
  output F2
);

  wire and_1_out, and_2_out, not_1_out, not_2_out, not_3_out, not_4_out, or_1_out, or_2_out, xor_1_out,
       xor_2_out;

  and and_1 (and_1_out, A1, B1);
  not not_1 (not_1_out, or_1_out);
  or or_1 (or_1_out, A1, B1);
  xor xor_1 (xor_1_out, A1, B1);
  not not_2 (not_2_out, A1);
  and and_2 (and_2_out, A2, B2);
  or or_2 (or_2_out, A2, B2);
  xor xor_2 (xor_2_out, A2, B2);
  not not_3 (not_3_out, A2);
  not not_4 (not_4_out, or_2_out);
  Multiplexer #(.select(2)) multiplexer_1 (
    .in0(and_1_out), .in1(not_1_out), .in2(xor_1_out), .in3(not_2_out), .out(F1), .sel(S1_S2));  // open: en
  Multiplexer #(.select(2)) multiplexer_2 (
    .in0(and_2_out), .in1(not_4_out), .in2(xor_2_out), .in3(not_3_out), .out(F2), .sel(S1_S2));  // open: en

  assign out_7 = {F2, F1};
endmodule

module subcircuit (
  input  A1,
  input  B1,
  input  A2,
  input  B2,
  input  [1:0] Select_Line,
  output [1:0] output_F1_F2
);

  main main_1 (.A1(A1), .B1(B1), .A2(A2), .B2(B2), .S1_S2(Select_Line), .out_7(output_F1_F2));  // open: F1, F2

  // Notes on the sheet:
  //   Subcircuit of 2 bit logic unit
endmodule
