// Logisim project circuit with subcirucit.circ as structural Verilog: 2 circuits, main circuit main
module main (
  input  A,
  input  B,
  input  [1:0] S1_S2,
  output \output 
);

  wire and_1_out, not_1_out, not_2_out, or_1_out, xor_1_out;

  and and_1 (and_1_out, A, B);
  not not_1 (not_1_out, or_1_out);
  or or_1 (or_1_out, A, B);
  xor xor_1 (xor_1_out, A, B);
  not not_2 (not_2_out, A);
  Multiplexer #(.select(2)) multiplexer_1 (
    .in0(and_1_out), .in1(not_1_out), .in2(xor_1_out), .in3(not_2_out), .out(\output ), .sel(S1_S2));  // open: en
endmodule

module subcircuit (
  input  A,
  input  B,
  input  \output ,
  input  [1:0] Select_Bits
);

  main main_1 (.A(A), .B(B), .S1_S2(Select_Bits), .\output (\output ));
endmodule
