// Logisim project lab 5 main.circ as structural Verilog: 1 circuit, main circuit main
module main (
  input  M,
  output C,
  output B,
  output A
);

  wire and_1_out, and_2_out, and_3_out, and_4_out, CLOCK_out, not_1_out, or_1_out, or_2_out, or_3_out,
       RESET_out, t_ff_1_qn, t_ff_2_qn, xor_1_out, xor_2_out, xor_3_out;

  and and_1 (and_1_out, not_1_out, t_ff_1_qn);
  and and_2 (and_2_out, and_1_out, t_ff_2_qn);
  not not_1 (not_1_out, M);
  and and_3 (and_3_out, M, C);
  and and_4 (and_4_out, and_3_out, B);
  or or_1 (or_1_out, M, not_1_out);
  or or_2 (or_2_out, and_4_out, and_2_out);
  or or_3 (or_3_out, and_3_out, and_1_out);
  xor xor_1 (xor_1_out, A, or_2_out);
  xor xor_2 (xor_2_out, C, or_1_out);
  xor xor_3 (xor_3_out, B, or_3_out);
  T_Flip_Flop t_ff_1 (.clk(CLOCK_out), .T(xor_2_out), .Q(C), .Qn(t_ff_1_qn), .reset(RESET_out));  // open: preset, en
  T_Flip_Flop t_ff_2 (.clk(CLOCK_out), .T(xor_3_out), .Q(B), .Qn(t_ff_2_qn), .reset(RESET_out));  // open: preset, en
  T_Flip_Flop t_ff_3 (.clk(CLOCK_out), .T(xor_1_out), .Q(A), .reset(RESET_out));  // open: Qn, preset, en
  Clock CLOCK (.out(CLOCK_out));
  Button RESET (.out(RESET_out));
endmodule
