// Logisim project lab 5.circ as structural Verilog: 1 circuit, main circuit main
module main (
  input  M,
  input  in_2,
  input  in_3,
  output out_4,
  output out_5,
  output out_6
);

  wire and_1_out, and_2_out, and_3_out, and_4_out, button_1_out, clock_1_out, not_1_out, or_1_out, or_2_out,
       TB_qn, TC_qn;

  not not_1 (not_1_out, M);
  Clock clock_1 (.out(clock_1_out));
  Button button_1 (.out(button_1_out));
  T_Flip_Flop TC (.clk(clock_1_out), .T(in_2), .Q(out_4), .Qn(TC_qn), .reset(button_1_out), .en(in_3));  // open: preset
  and and_1 (and_1_out, not_1_out, out_4);
  and and_2 (and_2_out, M, TC_qn);
  or or_1 (or_1_out, and_1_out, and_2_out);
  T_Flip_Flop TB (
    .clk(clock_1_out), .T(or_1_out), .Q(out_5), .Qn(TB_qn), .reset(button_1_out), .en(in_3));  // open: preset
  and and_3 (and_3_out, not_1_out, out_5, out_4);
  and and_4 (and_4_out, TC_qn, TB_qn, M);
  or or_2 (or_2_out, and_3_out, and_4_out);
  T_Flip_Flop TA (.clk(clock_1_out), .T(or_2_out), .Q(out_6), .reset(button_1_out), .en(in_3));  // open: Qn, preset
endmodule
