// Logisim project lab5 two.circ as structural Verilog: 1 circuit, main circuit main
module main (
  input  in_1,
  output out_2,
  output out_3,
  output out_4
);

  wire and_1_out, and_2_out, and_3_out, and_4_out, button_1_out, clock_1_out, not_1_out, or_1_out, or_2_out,
       or_3_out, t_ff_1_qn, t_ff_2_qn, undriven, undriven_2, xor_1_out, xor_2_out, xor_3_out;

  not not_1 (not_1_out, in_1);
  and and_1 (and_1_out, not_1_out, t_ff_1_qn);
  and and_2 (and_2_out, and_1_out, t_ff_2_qn);
  and and_3 (and_3_out, in_1, undriven_2);
  and and_4 (and_4_out, and_3_out, undriven);
  or or_1 (or_1_out, in_1, not_1_out);
  or or_2 (or_2_out, and_3_out, and_1_out);
  or or_3 (or_3_out, and_4_out, and_2_out);
  xor xor_1 (xor_1_out, undriven, or_2_out);
  xor xor_2 (xor_2_out, out_4, or_3_out);
  xor xor_3 (xor_3_out, undriven_2, or_1_out);
  Clock clock_1 (.out(clock_1_out));
  T_Flip_Flop t_ff_1 (.clk(clock_1_out), .T(xor_3_out), .Q(out_2), .Qn(t_ff_1_qn));  // open: preset, reset, en
  T_Flip_Flop t_ff_2 (.clk(clock_1_out), .T(xor_1_out), .Qn(t_ff_2_qn), .reset(button_1_out));  // open: Q, preset, en
  T_Flip_Flop t_ff_3 (.clk(clock_1_out), .T(xor_2_out), .Q(out_4), .reset(button_1_out));  // open: Qn, preset, en
  Button button_1 (.out(button_1_out));
endmodule
