// Logisim project Lab 6 2 bit register file.circ as structural Verilog: 1 circuit, main circuit main
module main (
  input  [1:0] Write_Data,
  input  [1:0] RS,
  input  Write_Enable,
  input  [1:0] RD,
  input  [1:0] RT,
  output [1:0] Read_Data_01,
  output [1:0] Read_Data_02
);

  wire clock_1_out, demultiplexer_1_out0, demultiplexer_1_out1, demultiplexer_1_out2, demultiplexer_1_out3;
  wire [1:0] register_1_q, register_2_q, register_3_q, register_4_q;

  Clock clock_1 (.out(clock_1_out));
  Demultiplexer #(.select(2), .enable("false")) demultiplexer_1 (
    .out0(demultiplexer_1_out0), .out1(demultiplexer_1_out1), .out2(demultiplexer_1_out2),
    .out3(demultiplexer_1_out3), .in(Write_Enable), .sel(RD));
  Register #(.width(2)) register_1 (
    .D(Write_Data), .en(demultiplexer_1_out0), .Q(register_1_q), .clk(clock_1_out));  // open: clr
  Register #(.width(2)) register_2 (
    .D(Write_Data), .en(demultiplexer_1_out1), .Q(register_2_q), .clk(clock_1_out));  // open: clr
  Register #(.width(2)) register_3 (
    .D(Write_Data), .en(demultiplexer_1_out2), .Q(register_3_q), .clk(clock_1_out));  // open: clr
  Register #(.width(2)) register_4 (
    .D(Write_Data), .en(demultiplexer_1_out3), .Q(register_4_q), .clk(clock_1_out));  // open: clr
  Multiplexer #(.select(2), .width(2), .enable("false")) multiplexer_1 (
    .in0(register_1_q), .in1(register_2_q), .in2(register_3_q), .in3(register_4_q), .out(Read_Data_01),
    .sel(RS));
  Multiplexer #(.select(2), .width(2), .enable("false")) multiplexer_2 (
    .in0(register_1_q), .in1(register_2_q), .in2(register_3_q), .in3(register_4_q), .out(Read_Data_02),
    .sel(RT));
endmodule
