// Logisim project 1bit and 16bit alu.circ as structural Verilog: 2 circuits, main circuit main
module main (
  input  Cin,
  input  Sub,
  input  B,
  input  A,
  input  [2:0] Opcode,
  output out_6,
  output out_7
);

  wire adder_1_out, and_1_out, comparator_1_eq, comparator_1_gt, comparator_1_lt, multiplier_1_out, or_1_out,
       xor_1_out, xor_2_out;

  xor xor_1 (xor_1_out, B, Sub);
  and and_1 (and_1_out, A, B);
  or or_1 (or_1_out, A, B);
  xor xor_2 (xor_2_out, A, B);
  Adder #(.width(1)) adder_1 (.a(A), .b(xor_1_out), .out(adder_1_out), .cin(Cin), .cout(out_7));
  Multiplier #(.width(1)) multiplier_1 (.a(A), .b(B), .out(multiplier_1_out), .cin(Cin));  // open: cout
  Comparator #(.width(1)) comparator_1 (.a(A), .b(B), .gt(comparator_1_gt), .eq(comparator_1_eq), .lt(comparator_1_lt));
  Multiplexer #(.select(3), .enable("false")) multiplexer_1 (
    .in0(and_1_out), .in1(or_1_out), .in2(xor_2_out), .in3(adder_1_out), .in4(multiplier_1_out),
    .in5(comparator_1_gt), .in6(comparator_1_eq), .in7(comparator_1_lt), .out(out_6), .sel(Opcode));
endmodule

module _16_bit (
  input  in_1,
  input  in_2,
  input  [15:0] in_3,
  input  [15:0] in_4,
  input  [2:0] in_5,
  output out_6,
  output [15:0] out_7
);

  wire main_1_out_7, main_2_out_7, main_3_out_7, main_4_out_7, main_5_out_7, main_6_out_7, main_7_out_7,
       main_8_out_7, main_9_out_7, main_10_out_7, main_11_out_7, main_12_out_7, main_13_out_7, main_14_out_7,
       main_15_out_7;

  main main_1 (
    .out_6(out_7[14]), .out_7(main_1_out_7), .Cin(in_1), .Sub(in_2), .B(in_3[14]), .A(in_4[14]), .Opcode(in_5));
  main main_2 (
    .out_6(out_7[15]), .out_7(main_2_out_7), .Cin(main_1_out_7), .Sub(in_2), .B(in_3[15]), .A(in_4[15]),
    .Opcode(in_5));
  main main_3 (
    .out_6(out_7[13]), .out_7(main_3_out_7), .Cin(main_2_out_7), .Sub(in_2), .B(in_3[13]), .A(in_4[13]),
    .Opcode(in_5));
  main main_4 (
    .out_6(out_7[12]), .out_7(main_4_out_7), .Cin(main_3_out_7), .Sub(in_2), .B(in_3[12]), .A(in_4[12]),
    .Opcode(in_5));
  main main_5 (
    .out_6(out_7[11]), .out_7(main_5_out_7), .Cin(main_4_out_7), .Sub(in_2), .B(in_3[11]), .A(in_4[11]),
    .Opcode(in_5));
  main main_6 (
    .out_6(out_7[10]), .out_7(main_6_out_7), .Cin(main_5_out_7), .Sub(in_2), .B(in_3[10]), .A(in_4[10]),
    .Opcode(in_5));
  main main_7 (
    .out_6(out_7[9]), .out_7(main_7_out_7), .Cin(main_6_out_7), .Sub(in_2), .B(in_3[9]), .A(in_4[9]),
    .Opcode(in_5));
  main main_8 (
    .out_6(out_7[8]), .out_7(main_8_out_7), .Cin(main_7_out_7), .Sub(in_2), .B(in_3[8]), .A(in_4[8]),
    .Opcode(in_5));
  main main_9 (
    .out_6(out_7[7]), .out_7(main_9_out_7), .Cin(main_8_out_7), .Sub(in_2), .B(in_3[7]), .A(in_4[7]),
    .Opcode(in_5));
  main main_10 (
    .out_6(out_7[6]), .out_7(main_10_out_7), .Cin(main_9_out_7), .Sub(in_2), .B(in_3[6]), .A(in_4[6]),
    .Opcode(in_5));
  main main_11 (
    .out_6(out_7[5]), .out_7(main_11_out_7), .Cin(main_10_out_7), .Sub(in_2), .B(in_3[5]), .A(in_4[5]),
    .Opcode(in_5));
  main main_12 (
    .out_6(out_7[4]), .out_7(main_12_out_7), .Cin(main_11_out_7), .Sub(in_2), .B(in_3[4]), .A(in_4[4]),
    .Opcode(in_5));
  main main_13 (
    .out_6(out_7[3]), .out_7(main_13_out_7), .Cin(main_12_out_7), .Sub(in_2), .B(in_3[3]), .A(in_4[3]),
    .Opcode(in_5));
  main main_14 (
    .out_6(out_7[2]), .out_7(main_14_out_7), .Cin(main_13_out_7), .Sub(in_2), .B(in_3[2]), .A(in_4[2]),
    .Opcode(in_5));
  main main_15 (
    .out_6(out_7[1]), .out_7(main_15_out_7), .Cin(main_14_out_7), .Sub(in_2), .B(in_3[1]), .A(in_4[1]),
    .Opcode(in_5));
  main main_16 (
    .out_6(out_7[0]), .out_7(out_6), .Cin(main_15_out_7), .Sub(in_2), .B(in_3[0]), .A(in_4[0]), .Opcode(in_5));
endmodule
