// Logisim project Lab 2 main and subcircuit.circ as structural Verilog: 2 circuits, main circuit main
module main (
  input  Cin,
  input  [1:0] Select_Bits,
  input  A0,
  input  B0,
  input  A1,
  input  B1,
  input  A2,
  input  B2,
  input  A3,
  input  B3,
  input  in_11,
  output [3:0] out_12,
  output out_13
);

  wire adder_1_cout, adder_2_cout, adder_3_cout, multiplexer_1_out, multiplexer_2_out, multiplexer_3_out,
       multiplexer_4_out, not_1_out, not_2_out, not_3_out, not_4_out, not_5_out;

  not not_1 (not_1_out, B0);
  not not_2 (not_2_out, B1);
  not not_3 (not_3_out, B2);
  not not_4 (not_4_out, B3);
  not not_5 (not_5_out, in_11);
  Multiplexer #(.select(2), .enable("false")) multiplexer_1 (
    .in0(B0), .in1(not_1_out), .in2(in_11), .in3(not_5_out), .out(multiplexer_1_out), .sel(Select_Bits));
  Multiplexer #(.select(2), .enable("false")) multiplexer_2 (
    .in0(B1), .in1(not_2_out), .in2(in_11), .in3(not_5_out), .out(multiplexer_2_out), .sel(Select_Bits));
  Multiplexer #(.select(2), .enable("false")) multiplexer_3 (
    .in0(B2), .in1(not_3_out), .in2(in_11), .in3(not_5_out), .out(multiplexer_3_out), .sel(Select_Bits));
  Multiplexer #(.select(2), .enable("false")) multiplexer_4 (
    .in0(B3), .in1(not_4_out), .in2(in_11), .in3(not_5_out), .out(multiplexer_4_out), .sel(Select_Bits));
  Adder #(.width(1)) adder_1 (.a(A0), .b(multiplexer_1_out), .out(out_12[0]), .cin(Cin), .cout(adder_1_cout));
  Adder #(.width(1)) adder_2 (.a(A1), .b(multiplexer_2_out), .out(out_12[1]), .cin(adder_1_cout), .cout(adder_2_cout));
  Adder #(.width(1)) adder_3 (.a(A2), .b(multiplexer_3_out), .out(out_12[2]), .cin(adder_2_cout), .cout(adder_3_cout));
  Adder #(.width(1)) adder_4 (.a(A3), .b(multiplexer_4_out), .out(out_12[3]), .cin(adder_3_cout), .cout(out_13));
endmodule

module subcircuit (
  input  in_1,
  input  [1:0] Select_Bits,
  input  B0,
  input  A0,
  input  A1,
  input  B1,
  input  A2,
  input  B2,
  input  A3,
  input  B3,
  input  in_11,
  output [3:0] \output ,
  output out_13
);

  main main_1 (
    .Cin(in_1), .Select_Bits(Select_Bits), .A0(A0), .B0(B0), .A1(A1), .B1(B1), .A2(A2), .B2(B2), .A3(A3),
    .B3(B3), .out_13(out_13), .in_11(in_11), .out_12(\output ));
endmodule
