// Logisim project Multiplier main, subcircuit and adder.circ as structural Verilog: 3 circuits, main circuit multiplier
module multiplier (
  input  A4,
  input  A3,
  input  A2,
  input  A1,
  input  B4,
  input  B3,
  input  B2,
  input  B1,
  input  in_9,
  input  in_10,
  input  in_11,
  input  in_12,
  output S2,
  output S4,
  output S3,
  output S1,
  output S7,
  output S0,
  output S6,
  output S5
);

  wire adder_2_cout, adder_2_s2, adder_2_s3, adder_2_s4, adder_3_cout, adder_3_s2, adder_3_s3, adder_3_s4,
       and_1_out, and_2_out, and_3_out, and_4_out, and_5_out, and_6_out, and_7_out, and_8_out, and_9_out,
       and_10_out, and_11_out, and_12_out, and_13_out, and_14_out, and_15_out;

  and and_1 (and_1_out, A4, B4);
  and and_2 (and_2_out, A4, B3);
  adder adder_1 (
    .A1(and_4_out), .B1(adder_2_s2), .A2(and_3_out), .B2(adder_2_s3), .A3(and_2_out), .B3(adder_2_s4),
    .A4(and_1_out), .B4(adder_2_cout), .Cin(in_12), .Cout(S7), .S1(S3), .S2(S4), .S3(S5), .S4(S6));
  and and_3 (and_3_out, A4, B2);
  and and_4 (and_4_out, A4, B1);
  and and_5 (and_5_out, A3, B4);
  and and_6 (and_6_out, A3, B3);
  and and_7 (and_7_out, A3, B2);
  adder adder_2 (
    .A1(and_8_out), .B1(adder_3_s2), .A2(and_7_out), .B2(adder_3_s3), .A3(and_6_out), .B3(adder_3_s4),
    .A4(and_5_out), .B4(adder_3_cout), .Cin(in_11), .Cout(adder_2_cout), .S1(S2), .S2(adder_2_s2),
    .S3(adder_2_s3), .S4(adder_2_s4));
  and and_8 (and_8_out, A3, B1);
  and and_9 (and_9_out, A2, B4);
  and and_10 (and_10_out, A2, B3);
  and and_11 (and_11_out, A2, B1);
  and and_12 (and_12_out, A2, B2);
  and and_13 (and_13_out, A1, B4);
  and and_14 (and_14_out, A1, B3);
  adder adder_3 (
    .A1(and_11_out), .B1(and_15_out), .A2(and_12_out), .B2(and_14_out), .A3(and_10_out), .B3(and_13_out),
    .A4(and_9_out), .B4(in_9), .Cin(in_10), .Cout(adder_3_cout), .S1(S1), .S2(adder_3_s2), .S3(adder_3_s3),
    .S4(adder_3_s4));
  and and_15 (and_15_out, A1, B2);
  and and_16 (S0, A1, B1);
endmodule

// Pre made Adder
module adder (
  input  Cin,
  input  A1,
  input  B1,
  input  A2,
  input  B2,
  input  A3,
  input  B3,
  input  A4,
  input  B4,
  output S1,
  output S2,
  output S3,
  output S4,
  output Cout
);

  wire adder_1_cout, adder_2_cout, adder_3_cout;

  Adder #(.width(1)) adder_1 (.a(A1), .b(B1), .out(S1), .cin(Cin), .cout(adder_1_cout));
  Adder #(.width(1)) adder_2 (.a(A2), .b(B2), .out(S2), .cin(adder_1_cout), .cout(adder_2_cout));
  Adder #(.width(1)) adder_3 (.a(A3), .b(B3), .out(S3), .cin(adder_2_cout), .cout(adder_3_cout));
  Adder #(.width(1)) adder_4 (.a(A4), .b(B4), .out(S4), .cin(adder_3_cout), .cout(Cout));
endmodule

module Multiplier_Subcircuit (
  input  B4,
  input  A1,
  input  A2,
  input  A3,
  input  B3,
  input  A4,
  input  B2,
  input  B1,
  input  in_9,
  output [7:0] Outputs_S0_S7
);

  multiplier multiplier_1 (
    .in_9(in_9), .A4(A4), .A3(A3), .A2(A2), .A1(A1), .B4(B4), .B3(B3), .B2(B2), .B1(B1),
    .S7(Outputs_S0_S7[7]), .S6(Outputs_S0_S7[6]), .S5(Outputs_S0_S7[5]), .S4(Outputs_S0_S7[4]),
    .S3(Outputs_S0_S7[3]), .S2(Outputs_S0_S7[2]), .S1(Outputs_S0_S7[1]), .S0(Outputs_S0_S7[0]));  // open: in_10, in_11, in_12
endmodule
