// Logisim project multiplier exam.circ as structural Verilog: 1 circuit, main circuit main
module main (
  input  [3:0] A,
  input  [4:0] B,
  output [7:0] Outputs_S1_S8
);

  wire adder_1_cout, adder_1_out, adder_2_cout, adder_2_out, adder_3_out, adder_4_cout, adder_5_cout,
       adder_5_out, adder_6_cout, adder_6_out, adder_7_cout, adder_7_out, adder_8_cout, adder_9_cout,
       adder_9_out, adder_11_cout, adder_12_cout, adder_13_cout, and_1_out, and_2_out, and_3_out, and_5_out,
       and_6_out, and_7_out, and_8_out, and_9_out, and_10_out, and_11_out, and_12_out, and_13_out,
       and_14_out, and_15_out, and_16_out, and_17_out, and_18_out;

  and and_1 (and_1_out, A[1], B[1]);
  and and_2 (and_2_out, A[2], B[1]);
  and and_3 (and_3_out, A[3], B[1]);
  and and_4 (Outputs_S1_S8[0], A[0], B[1]);
  and and_5 (and_5_out, A[0], B[2]);
  and and_6 (and_6_out, A[1], B[2]);
  and and_7 (and_7_out, A[3], B[2]);
  and and_8 (and_8_out, A[2], B[0]);
  Adder #(.width(1)) adder_1 (.a(and_2_out), .b(and_6_out), .out(adder_1_out), .cin(adder_4_cout), .cout(adder_1_cout));
  and and_9 (and_9_out, A[2], B[2]);
  Adder #(.width(1)) adder_2 (.a(adder_5_cout), .b(and_7_out), .out(adder_2_out), .cin(1'b0), .cout(adder_2_cout));
  and and_10 (and_10_out, A[3], B[3]);
  Adder #(.width(1)) adder_3 (.a(adder_7_cout), .b(and_8_out), .out(adder_3_out), .cin(1'b0));  // open: cout
  Adder #(.width(1)) adder_4 (.a(and_1_out), .b(and_5_out), .out(Outputs_S1_S8[1]), .cin(1'b0), .cout(adder_4_cout));
  Adder #(.width(1)) adder_5 (.a(and_3_out), .b(and_9_out), .out(adder_5_out), .cin(adder_1_cout), .cout(adder_5_cout));
  and and_11 (and_11_out, A[0], B[3]);
  and and_12 (and_12_out, A[2], B[3]);
  and and_13 (and_13_out, A[1], B[0]);
  and and_14 (and_14_out, A[1], B[3]);
  Adder #(.width(1)) adder_6 (
    .a(adder_2_out), .b(and_12_out), .out(adder_6_out), .cin(adder_9_cout), .cout(adder_6_cout));
  Adder #(.width(1)) adder_7 (
    .a(adder_2_cout), .b(and_10_out), .out(adder_7_out), .cin(adder_6_cout), .cout(adder_7_cout));
  Adder #(.width(1)) adder_8 (.a(adder_1_out), .b(and_11_out), .out(Outputs_S1_S8[2]), .cin(1'b0), .cout(adder_8_cout));
  Adder #(.width(1)) adder_9 (
    .a(adder_5_out), .b(and_14_out), .out(adder_9_out), .cin(adder_8_cout), .cout(adder_9_cout));
  Adder #(.width(1)) adder_10 (
    .a(adder_3_out), .b(and_13_out), .out(Outputs_S1_S8[6]), .cin(adder_7_cout));  // open: cout
  and and_15 (and_15_out, A[1], B[4]);
  and and_16 (and_16_out, A[0], B[4]);
  and and_17 (and_17_out, A[2], B[4]);
  and and_18 (and_18_out, A[0], B[0]);
  Adder #(.width(1)) adder_11 (
    .a(adder_9_out), .b(and_16_out), .out(Outputs_S1_S8[3]), .cin(1'b0), .cout(adder_11_cout));
  Adder #(.width(1)) adder_12 (
    .a(adder_6_out), .b(and_15_out), .out(Outputs_S1_S8[4]), .cin(adder_11_cout), .cout(adder_12_cout));
  Adder #(.width(1)) adder_13 (
    .a(adder_7_out), .b(and_17_out), .out(Outputs_S1_S8[5]), .cin(adder_12_cout), .cout(adder_13_cout));
  Adder #(.width(1)) adder_14 (
    .a(Outputs_S1_S8[5]), .b(and_18_out), .out(Outputs_S1_S8[7]), .cin(adder_13_cout));  // open: cout

  // Other names for the same wires on the sheet: A1 = A[0]; A2 = A[1]; A3 = A[2]; A4 = A[3]; B5 = B[0]

  // Notes on the sheet:
  //   4 x 5 multiplier
  //   As 100 can not be higher than 8 bits and 30 can not be higher than 5 bits
endmodule
