// Logisim project datapath.circ as structural Verilog: 4 circuits, main circuit main
module main (
  input  in_1,
  input  SW,
  input  LW,
  input  in_4,
  input  R___I,
  input  R___I_2,
  input  Select,
  input  Clr,
  input  Mem_ALU_R,
  input  R_I,
  output [3:0] RD,
  output [15:0] out_12,
  output [15:0] out_13,
  output [3:0] RT,
  output [3:0] RS,
  output [15:0] out_16,
  output [3:0] opcode,
  output [1:0] out_18
);

  wire clock_1_out;
  wire [3:0] multiplexer_1_out;
  wire [15:0] adder_1_out, bit_extender_1_out, multiplexer_2_out, multiplexer_3_out, ram_1_data, register_1_q;

  Register #(.width(16)) register_1 (.D(adder_1_out), .Q(register_1_q), .clk(clock_1_out), .clr(in_4));  // open: en
  Clock clock_1 (.out(clock_1_out));
  Adder #(.width(16)) adder_1 (.a(register_1_q), .b(16'h1), .out(adder_1_out));  // open: cin, cout
  ROM #(.addrWidth(16), .dataWidth(16)) rom_1 (.addr(register_1_q), .data({opcode, RS, RT, RD}));  // open: sel
  Multiplexer #(.width(4), .enable("false")) multiplexer_1 (.in0(RT), .in1(RD), .out(multiplexer_1_out), .sel(R___I));
  assign bit_extender_1_out = {{12{1'b0}}, RD};  // Bit_Extender bit_extender_1
  _16_bit_register_file u_16_bit_register_file_1 (
    .Write_Data(multiplexer_3_out), .Write_Enable(clock_1_out), .RD(multiplexer_1_out),
    .Read_Data_01(out_12), .Read_Data_02(out_16), .RS(RS), .RT(RT), .in_5(R_I));
  Bit_Extender #(.in_width(4), .out_width(2)) bit_extender_2 (.in(opcode), .out(out_18));
  Multiplexer #(.width(16), .enable("false")) multiplexer_2 (
    .in0(out_16), .in1(bit_extender_1_out), .out(multiplexer_2_out), .sel(R___I_2));
  _16_bit_alu u_16_bit_alu_1 (
    .A(out_12), .B(multiplexer_2_out), .opcode(out_18), .Cin(in_1), .Result(out_13));  // open: Overflow, Cout, Zero_Signal
  RAM #(.addrWidth(16), .dataWidth(16), .bus("separate")) ram_1 (
    .addr(out_13), .din(bit_extender_1_out), .data(ram_1_data), .str(SW), .sel(Select), .clk(clock_1_out),
    .ld(LW), .clr(Clr));
  Multiplexer #(.width(16), .enable("false")) multiplexer_3 (
    .in0(ram_1_data), .in1(out_13), .out(multiplexer_3_out), .sel(Mem_ALU_R));

  // Notes on the sheet:
  //   Instruction Memory
  //   Instruction Fetch
  //   contents of rom_1 (hex, n*v repeats v):
  //   2241
  //   Instruction Decode
  //   Execute
  //   Accessed primary memory
  //   Write Back
endmodule

module _1_bit_alu (
  input  Cin,
  input  A,
  input  B,
  input  [1:0] Opcode,
  output Output,
  output Overflow,
  output Zero_signal,
  output Cout
);

  wire adder_1_out, and_1_out, or_1_out, subtractor_1_out;

  and and_1 (and_1_out, A, B);
  or or_1 (or_1_out, A, B);
  Adder #(.width(1)) adder_1 (.a(A), .b(B), .out(adder_1_out), .cin(Cin), .cout(Cout));
  Subtractor #(.width(1)) subtractor_1 (.a(A), .b(B), .out(subtractor_1_out));  // open: bin, bout
  Multiplexer #(.select(2), .enable("false")) multiplexer_1 (
    .in0(and_1_out), .in1(or_1_out), .in2(adder_1_out), .in3(subtractor_1_out), .out(Output), .sel(Opcode));
  xor xor_1 (Overflow, Output, Cout);
  nor nor_1 (Zero_signal, Output, Cout);
endmodule

module _16_bit_register_file (
  input  [15:0] Write_Data,
  input  Write_Enable,
  input  [3:0] RS,
  input  [3:0] RD,
  input  in_5,
  input  [3:0] RT,
  output [15:0] Read_Data_01,
  output [15:0] Read_Data_02
);

  wire demultiplexer_1_out0, demultiplexer_1_out1, demultiplexer_1_out2, demultiplexer_1_out3,
       demultiplexer_1_out4, demultiplexer_1_out5, demultiplexer_1_out6, demultiplexer_1_out7,
       demultiplexer_1_out8, demultiplexer_1_out9, demultiplexer_1_out10, demultiplexer_1_out11,
       demultiplexer_1_out12, demultiplexer_1_out13, demultiplexer_1_out14, demultiplexer_1_out15;
  wire [15:0] register_1_q, register_2_q, register_3_q, register_4_q, register_5_q, register_6_q,
       register_7_q, register_8_q, register_9_q, register_10_q, register_11_q, register_12_q, register_13_q,
       register_14_q, register_15_q, register_16_q;

  Demultiplexer #(.select(4)) demultiplexer_1 (
    .out0(demultiplexer_1_out0), .out1(demultiplexer_1_out1), .out2(demultiplexer_1_out2),
    .out3(demultiplexer_1_out3), .out4(demultiplexer_1_out4), .out5(demultiplexer_1_out5),
    .out6(demultiplexer_1_out6), .out7(demultiplexer_1_out7), .out8(demultiplexer_1_out8),
    .out9(demultiplexer_1_out9), .out10(demultiplexer_1_out10), .out11(demultiplexer_1_out11),
    .out12(demultiplexer_1_out12), .out13(demultiplexer_1_out13), .out14(demultiplexer_1_out14),
    .out15(demultiplexer_1_out15), .in(Write_Enable), .sel(RD));  // open: en
  Register #(.width(16)) register_1 (
    .D(Write_Data), .en(demultiplexer_1_out0), .Q(register_1_q), .clk(in_5));  // open: clr
  Register #(.width(16)) register_2 (
    .D(Write_Data), .en(demultiplexer_1_out1), .Q(register_2_q), .clk(in_5));  // open: clr
  Register #(.width(16)) register_3 (
    .D(Write_Data), .en(demultiplexer_1_out2), .Q(register_3_q), .clk(in_5));  // open: clr
  Register #(.width(16)) register_4 (
    .D(Write_Data), .en(demultiplexer_1_out3), .Q(register_4_q), .clk(in_5));  // open: clr
  Register #(.width(16)) register_5 (
    .D(Write_Data), .en(demultiplexer_1_out4), .Q(register_5_q), .clk(in_5));  // open: clr
  Register #(.width(16)) register_6 (
    .D(Write_Data), .en(demultiplexer_1_out5), .Q(register_6_q), .clk(in_5));  // open: clr
  Register #(.width(16)) register_7 (
    .D(Write_Data), .en(demultiplexer_1_out6), .Q(register_7_q), .clk(in_5));  // open: clr
  Register #(.width(16)) register_8 (
    .D(Write_Data), .en(demultiplexer_1_out7), .Q(register_8_q), .clk(in_5));  // open: clr
  Register #(.width(16)) register_9 (
    .D(Write_Data), .en(demultiplexer_1_out8), .Q(register_9_q), .clk(in_5));  // open: clr
  Register #(.width(16)) register_10 (
    .D(Write_Data), .en(demultiplexer_1_out9), .Q(register_10_q), .clk(in_5));  // open: clr
  Register #(.width(16)) register_11 (
    .D(Write_Data), .en(demultiplexer_1_out10), .Q(register_11_q), .clk(in_5));  // open: clr
  Register #(.width(16)) register_12 (
    .D(Write_Data), .en(demultiplexer_1_out11), .Q(register_12_q), .clk(in_5));  // open: clr
  Register #(.width(16)) register_13 (
    .D(Write_Data), .en(demultiplexer_1_out12), .Q(register_13_q), .clk(in_5));  // open: clr
  Register #(.width(16)) register_14 (
    .D(Write_Data), .en(demultiplexer_1_out13), .Q(register_14_q), .clk(in_5));  // open: clr
  Register #(.width(16)) register_15 (
    .D(Write_Data), .en(demultiplexer_1_out14), .Q(register_15_q), .clk(in_5));  // open: clr
  Register #(.width(16)) register_16 (
    .D(Write_Data), .en(demultiplexer_1_out15), .Q(register_16_q), .clk(in_5));  // open: clr
  Multiplexer #(.select(4), .width(16)) multiplexer_1 (
    .in0(register_1_q), .in1(register_2_q), .in2(register_3_q), .in3(register_4_q), .in4(register_5_q),
    .in5(register_6_q), .in6(register_7_q), .in7(register_8_q), .in8(register_9_q), .in9(register_10_q),
    .in10(register_11_q), .in11(register_12_q), .in12(register_13_q), .in13(register_14_q),
    .in14(register_15_q), .in15(register_16_q), .out(Read_Data_01), .sel(RS));  // open: en
  Multiplexer #(.select(4), .width(16)) multiplexer_2 (
    .in0(register_1_q), .in1(register_2_q), .in2(register_3_q), .in3(register_4_q), .in4(register_5_q),
    .in5(register_6_q), .in6(register_7_q), .in7(register_8_q), .in8(register_9_q), .in9(register_10_q),
    .in10(register_11_q), .in11(register_12_q), .in12(register_13_q), .in13(register_14_q),
    .in14(register_15_q), .in15(register_16_q), .out(Read_Data_02), .sel(RT));  // open: en
endmodule

module _16_bit_alu (
  input  Cin,
  input  [1:0] opcode,
  input  [15:0] A,
  input  [15:0] B,
  output Cout,
  output [15:0] Overflow,
  output [15:0] Result,
  output [15:0] Zero_Signal
);

  wire n1_bit_alu_1_cout, n1_bit_alu_2_cout, n1_bit_alu_3_cout, n1_bit_alu_4_cout, n1_bit_alu_5_cout,
       n1_bit_alu_6_cout, n1_bit_alu_7_cout, n1_bit_alu_8_cout, n1_bit_alu_9_cout, n1_bit_alu_10_cout,
       n1_bit_alu_11_cout, n1_bit_alu_12_cout, n1_bit_alu_13_cout, n1_bit_alu_14_cout, n1_bit_alu_15_cout;

  _1_bit_alu u_1_bit_alu_1 (
    .Output(Result[0]), .Overflow(Overflow[15]), .Zero_signal(Zero_Signal[0]), .Cout(n1_bit_alu_1_cout),
    .Cin(Cin), .A(B[0]), .B(A[0]), .Opcode(opcode));
  _1_bit_alu u_1_bit_alu_2 (
    .Output(Result[1]), .Overflow(Overflow[14]), .Zero_signal(Zero_Signal[1]), .Cout(n1_bit_alu_2_cout),
    .Cin(n1_bit_alu_1_cout), .A(B[1]), .B(A[1]), .Opcode(opcode));
  _1_bit_alu u_1_bit_alu_3 (
    .Output(Result[2]), .Overflow(Overflow[13]), .Zero_signal(Zero_Signal[2]), .Cout(n1_bit_alu_3_cout),
    .Cin(n1_bit_alu_2_cout), .A(B[2]), .B(A[2]), .Opcode(opcode));
  _1_bit_alu u_1_bit_alu_4 (
    .Output(Result[3]), .Overflow(Overflow[12]), .Zero_signal(Zero_Signal[3]), .Cout(n1_bit_alu_4_cout),
    .Cin(n1_bit_alu_3_cout), .A(B[3]), .B(A[3]), .Opcode(opcode));
  _1_bit_alu u_1_bit_alu_5 (
    .Output(Result[4]), .Overflow(Overflow[11]), .Zero_signal(Zero_Signal[4]), .Cout(n1_bit_alu_5_cout),
    .Cin(n1_bit_alu_4_cout), .A(B[4]), .B(A[4]), .Opcode(opcode));
  _1_bit_alu u_1_bit_alu_6 (
    .Output(Result[5]), .Overflow(Overflow[10]), .Zero_signal(Zero_Signal[5]), .Cout(n1_bit_alu_6_cout),
    .Cin(n1_bit_alu_5_cout), .A(B[5]), .B(A[5]), .Opcode(opcode));
  _1_bit_alu u_1_bit_alu_7 (
    .Output(Result[6]), .Overflow(Overflow[9]), .Zero_signal(Zero_Signal[6]), .Cout(n1_bit_alu_7_cout),
    .Cin(n1_bit_alu_6_cout), .A(B[6]), .B(A[6]), .Opcode(opcode));
  _1_bit_alu u_1_bit_alu_8 (
    .Output(Result[7]), .Overflow(Overflow[8]), .Zero_signal(Zero_Signal[7]), .Cout(n1_bit_alu_8_cout),
    .Cin(n1_bit_alu_7_cout), .A(B[7]), .B(A[7]), .Opcode(opcode));
  _1_bit_alu u_1_bit_alu_9 (
    .Output(Result[8]), .Overflow(Overflow[7]), .Zero_signal(Zero_Signal[8]), .Cout(n1_bit_alu_9_cout),
    .Cin(n1_bit_alu_8_cout), .A(B[8]), .B(A[8]), .Opcode(opcode));
  _1_bit_alu u_1_bit_alu_10 (
    .Output(Result[9]), .Overflow(Overflow[6]), .Zero_signal(Zero_Signal[9]), .Cout(n1_bit_alu_10_cout),
    .Cin(n1_bit_alu_9_cout), .A(B[9]), .B(A[9]), .Opcode(opcode));
  _1_bit_alu u_1_bit_alu_11 (
    .Output(Result[10]), .Overflow(Overflow[5]), .Zero_signal(Zero_Signal[10]), .Cout(n1_bit_alu_11_cout),
    .Cin(n1_bit_alu_10_cout), .A(B[10]), .B(A[10]), .Opcode(opcode));
  _1_bit_alu u_1_bit_alu_12 (
    .Output(Result[11]), .Overflow(Overflow[4]), .Zero_signal(Zero_Signal[11]), .Cout(n1_bit_alu_12_cout),
    .Cin(n1_bit_alu_11_cout), .A(B[11]), .B(A[11]), .Opcode(opcode));
  _1_bit_alu u_1_bit_alu_13 (
    .Output(Result[12]), .Overflow(Overflow[3]), .Zero_signal(Zero_Signal[12]), .Cout(n1_bit_alu_13_cout),
    .Cin(n1_bit_alu_12_cout), .A(B[12]), .B(A[12]), .Opcode(opcode));
  _1_bit_alu u_1_bit_alu_14 (
    .Output(Result[13]), .Overflow(Overflow[2]), .Zero_signal(Zero_Signal[13]), .Cout(n1_bit_alu_14_cout),
    .Cin(n1_bit_alu_13_cout), .A(B[13]), .B(A[13]), .Opcode(opcode));
  _1_bit_alu u_1_bit_alu_15 (
    .Output(Result[14]), .Overflow(Overflow[1]), .Zero_signal(Zero_Signal[14]), .Cout(n1_bit_alu_15_cout),
    .Cin(n1_bit_alu_14_cout), .A(B[14]), .B(A[14]), .Opcode(opcode));
  _1_bit_alu u_1_bit_alu_16 (
    .Output(Result[15]), .Overflow(Overflow[0]), .Zero_signal(Zero_Signal[15]), .Cout(Cout),
    .Cin(n1_bit_alu_15_cout), .A(B[15]), .B(A[15]), .Opcode(opcode));
endmodule
